// Logisim project Chairs and Sprinklers.circ as structural Verilog: 1 circuit, main circuit main
module main (
  input  x,
  input  PR,
  input  PR_2
);

  wire and_1_out, and_2_out, and_3_out, and_4_out, and_5_out, clk_2_out, clk_out, clock_1_out, d_ff_1_q,
       d_ff_1_qn, d_ff_2_q, d_ff_2_qn, d_ff_3_q, d_ff_3_qn, d_ff_4_q, d_ff_4_qn, d_ff_5_q, d_ff_5_qn,
       d_ff_6_q, d_ff_7_q, d_ff_8_q, d_ff_8_qn, not_1_out, not_2_out;

  and and_1 (and_1_out, not_1_out, not_2_out);
  not not_1 (not_1_out, and_2_out);
  and and_2 (and_2_out, d_ff_2_q, d_ff_5_qn, x);
  Clock #(.highDuration(2), .lowDuration(2)) clock_1 (.out(clock_1_out));
  Clock clk (.out(clk_out));
  and and_3 (and_3_out, d_ff_2_qn, d_ff_5_q);
  LED led_1 (.in(d_ff_1_q));
  D_Flip_Flop d_ff_1 (
    .clk(clk_out), .D(d_ff_4_qn), .Q(d_ff_1_q), .Qn(d_ff_1_qn), .preset(PR), .en(and_2_out));  // open: reset
  LED led_2 (.in(d_ff_1_qn));
  D_Flip_Flop d_ff_2 (
    .clk(clock_1_out), .D(and_3_out), .Q(d_ff_2_q), .Qn(d_ff_2_qn), .en(and_1_out));  // open: preset, reset
  LED led_3 (.in(d_ff_3_q));
  D_Flip_Flop d_ff_3 (
    .clk(clk_out), .D(d_ff_1_q), .Q(d_ff_3_q), .Qn(d_ff_3_qn), .preset(PR), .en(and_2_out));  // open: reset
  LED led_4 (.in(d_ff_3_qn));
  LED led_5 (.in(d_ff_4_q));
  D_Flip_Flop d_ff_4 (
    .clk(clk_out), .D(d_ff_3_q), .Q(d_ff_4_q), .Qn(d_ff_4_qn), .preset(PR), .en(and_2_out));  // open: reset
  LED led_6 (.in(d_ff_4_qn));
  and and_4 (and_4_out, x, d_ff_2_qn);
  D_Flip_Flop d_ff_5 (
    .clk(clock_1_out), .D(and_4_out), .Q(d_ff_5_q), .Qn(d_ff_5_qn), .en(and_1_out));  // open: preset, reset
  not not_2 (not_2_out, and_5_out);
  Clock clk_2 (.out(clk_2_out));
  and and_5 (and_5_out, d_ff_2_q, x, d_ff_5_q);
  D_Flip_Flop d_ff_6 (.clk(clk_2_out), .D(d_ff_8_qn), .Q(d_ff_6_q), .preset(PR_2), .en(and_5_out));  // open: Qn, reset
  LED led_7 (.in(d_ff_6_q));
  D_Flip_Flop d_ff_7 (.clk(clk_2_out), .D(d_ff_6_q), .Q(d_ff_7_q), .preset(PR_2), .en(and_5_out));  // open: Qn, reset
  LED led_8 (.in(d_ff_7_q));
  D_Flip_Flop d_ff_8 (
    .clk(clk_2_out), .D(d_ff_7_q), .Q(d_ff_8_q), .Qn(d_ff_8_qn), .preset(PR_2), .en(and_5_out));  // open: reset
  LED led_9 (.in(d_ff_8_q));

  // Notes on the sheet:
  //   SPRINKLERS
  //   DELUXE RIDE
  //   CHAIRS
  //   SPRINKLERS
  //   CLASSIC RIDE
endmodule
