// Logisim project Sequence.circ as structural Verilog: 1 circuit, main circuit main
module main (
  input  in_1,
  input  in_2,
  output out_3,
  output out_4
);

  wire and_1_out, and_2_out, and_4_out, and_5_out, clock_1_out, d_ff_1_q, d_ff_1_qn, d_ff_2_q, d_ff_2_qn,
       d_ff_3_q, d_ff_3_qn, not_1_out, or_1_out, or_2_out, xnor_1_out;

  not not_1 (not_1_out, in_1);
  Clock #(.highDuration(3)) clock_1 (.out(clock_1_out));
  D_Flip_Flop d_ff_1 (
    .clk(clock_1_out), .D(and_1_out), .Q(d_ff_1_q), .Qn(d_ff_1_qn), .en(in_2));  // open: preset, reset
  D_Flip_Flop d_ff_2 (.clk(clock_1_out), .D(or_1_out), .Q(d_ff_2_q), .Qn(d_ff_2_qn), .en(in_2));  // open: preset, reset
  D_Flip_Flop d_ff_3 (.clk(clock_1_out), .D(or_2_out), .Q(d_ff_3_q), .Qn(d_ff_3_qn), .en(in_2));  // open: preset, reset
  and and_1 (and_1_out, not_1_out, d_ff_1_qn, d_ff_2_qn, d_ff_3_qn);
  and and_2 (and_2_out, d_ff_1_qn, d_ff_2_qn, in_1);
  and and_3 (out_3, in_1, d_ff_1_qn, d_ff_2_q, d_ff_3_qn);
  and and_4 (and_4_out, d_ff_1_qn, d_ff_2_qn, d_ff_3_q);
  and and_5 (and_5_out, d_ff_3_qn, d_ff_1_q, d_ff_2_qn, not_1_out);
  xnor xnor_1 (xnor_1_out, in_1, d_ff_3_q);
  or or_1 (or_1_out, and_4_out, and_5_out);
  or or_2 (or_2_out, and_5_out, and_2_out);
  and and_6 (out_4, d_ff_2_q, d_ff_1_qn, xnor_1_out);
endmodule
