// Logisim project Sprinklers_Out.circ as structural Verilog: 1 circuit, main circuit main
module main (
  input  in_1
);

  wire and_1_out, and_2_out, and_3_out, clock_1_out, clock_2_out, clock_3_out, d_ff_1_qn, d_ff_2_q,
       d_ff_2_qn, d_ff_3_q, d_ff_3_qn, d_ff_4_q, d_ff_4_qn, d_ff_5_qn, d_ff_6_qn, d_ff_7_q, d_ff_7_qn,
       not_1_out, or_1_out, or_2_out, or_3_out, or_4_out;

  Clock clock_1 (.out(clock_1_out));
  not not_1 (not_1_out, d_ff_2_q);
  LED led_1 (.in(or_1_out));
  or or_1 (or_1_out, d_ff_4_q, and_2_out);
  D_Flip_Flop d_ff_1 (
    .clk(clock_1_out), .D(d_ff_1_qn), .Qn(d_ff_1_qn), .en(not_1_out), .reset(d_ff_2_q));  // open: Q, preset
  or or_2 (or_2_out, and_2_out, and_1_out);
  LED led_2 (.in(or_2_out));
  Clock #(.highDuration(8), .lowDuration(8)) clock_2 (.out(clock_2_out));
  D_Flip_Flop d_ff_2 (
    .clk(clock_2_out), .D(d_ff_2_qn), .Q(d_ff_2_q), .Qn(d_ff_2_qn), .en(in_1));  // open: preset, reset
  and and_1 (and_1_out, d_ff_4_qn, d_ff_3_q);
  D_Flip_Flop d_ff_3 (
    .clk(d_ff_1_qn), .D(d_ff_3_qn), .Q(d_ff_3_q), .Qn(d_ff_3_qn), .en(not_1_out), .reset(d_ff_2_q));  // open: preset
  D_Flip_Flop d_ff_4 (
    .clk(d_ff_3_qn), .D(d_ff_4_qn), .Q(d_ff_4_q), .Qn(d_ff_4_qn), .en(not_1_out), .reset(d_ff_2_q));  // open: preset
  and and_2 (and_2_out, not_1_out, d_ff_4_qn, d_ff_3_qn);
  Clock clock_3 (.out(clock_3_out));
  D_Flip_Flop d_ff_5 (
    .clk(clock_3_out), .D(d_ff_5_qn), .Qn(d_ff_5_qn), .preset(not_1_out), .en(d_ff_2_q));  // open: Q, reset
  or or_3 (or_3_out, and_2_out, d_ff_7_qn);
  LED led_3 (.in(or_3_out));
  D_Flip_Flop d_ff_6 (
    .clk(d_ff_5_qn), .D(d_ff_6_qn), .Qn(d_ff_6_qn), .preset(not_1_out), .en(d_ff_2_q));  // open: Q, reset
  and and_3 (and_3_out, d_ff_6_qn, d_ff_7_q);
  or or_4 (or_4_out, and_2_out, and_3_out);
  LED led_4 (.in(or_4_out));
  D_Flip_Flop d_ff_7 (
    .clk(d_ff_6_qn), .D(d_ff_7_qn), .Q(d_ff_7_q), .Qn(d_ff_7_qn), .preset(not_1_out), .en(d_ff_2_q));  // open: reset
endmodule
